# Fritzing sketch fritzing (saved by Fritzing 1.0.3b)

parts:
  Part1 = Adafruit ESP32-S3 Feather [part_number="Adafruit #5323"]
  Adafruit_3_5_inch_480x320_Capacitive_Touch_Display1 = Adafruit 3.5 inch 480x320 Capacitive Touch Display [part_number=#5846]

nets:
  N1: Part1.MISO, Adafruit_3_5_inch_480x320_Capacitive_Touch_Display1.SDO
  N2: Part1.MOSI, Adafruit_3_5_inch_480x320_Capacitive_Touch_Display1.SDI_5V
  N3: Part1.SCK, Adafruit_3_5_inch_480x320_Capacitive_Touch_Display1.LCD_WR_5V
  GND: Part1.GND, Adafruit_3_5_inch_480x320_Capacitive_Touch_Display1.GND
  3.3V: Part1.3.3V, Adafruit_3_5_inch_480x320_Capacitive_Touch_Display1.+5V
  N4: Part1.D10, Adafruit_3_5_inch_480x320_Capacitive_Touch_Display1.LCD_CS_5V
  N5: Part1.D6, Adafruit_3_5_inch_480x320_Capacitive_Touch_Display1.LCD_RS_5V

custom parts:
  Adafruit ESP32-S3 Feather: The ESP32-S3 has arrived in Feather format - and what a great way to get started with this powerful new chip from Espressif! With dual 240 MHz cores, WiFi and BLE support, and native USB, this Feather is great for powering your IoT projects. That's right - it's the new Adafruit ESP32-S3 Feather! With native USB and 8 MB flash, this board will let you upgrade your existing ESP32 projects.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
  Adafruit 3.5 inch 480x320 Capacitive Touch Display: Add some jazz & pizazz to your project with a color touchscreen LCD. This TFT display is big (3.5" diagonal) bright (6 white-LED backlight) and colorful! 480x320 pixels with individual RGB pixel control, this has way more resolution than a black and white 128x64 display, and double our 2.8" TFT. As a bonus, this display has a capacitive touchscreen attached to it already, so you can detect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
